# Fritzing sketch FilterBoxForKit (saved by Fritzing 0.9.3b)
stripboards: 1

parts:
  Part1 = Arduino Pro Mini v13
  R1 = Photocell (LDR) [package=THT]
  NRF24L1 = NRF24L01
  U2 = SWITCH_SPDT [package=kps-1290]
  S1 = Round Pushbutton
  S2 = Round Pushbutton
  J1 = Basic Force Sensing Resistor (FSR) [package=THT]
  R3 = Resistor [tolerance=±5% resistance=10k package="1206 [SMD]"]
  R2 = Resistor [tolerance=±5% resistance=10k package="1206 [SMD]"]
  BAT1 = BC9VPC [package=bc9vpc]

nets:
  VCC: Part1.VCC, R1.pin_0, NRF24L1.VCC, J1.pin_1
  N1: Part1.RAW, U2.P
  GND: Part1.A1, Part1.GND, NRF24L1.GND, S1.leg0, R3.Pin_1, R2.Pin_1, BAT1.V+
  N2: Part1.A0, J1.pin_0, R3.Pin_0
  N3: Part1.D13/SCK, NRF24L1.SCK
  N4: Part1.D12/MISO, NRF24L1.MISO
  N5: Part1.D11_PWM/MOSI, NRF24L1.MOSI
  N6: Part1.D10_PWM/SS, NRF24L1.CSN
  N7: Part1.D9_PWM, NRF24L1.CE
  N8: Part1.D4, S2.leg1
  N9: Part1.D3_PWM, S1.leg1
  N10: U2.S, BAT1.V-

notes:
  Pro Mini 3.3v 8mHz 328 chipset
  NRF connections
  1 - GND
  2 - VCC 3.3V !!! NOT 5V
  3 - CE to Arduino pin 9
  4 - CSN to Arduino pin 10
  5 - SCK to Arduino pin 13
  6 - MOSI to Arduino pin 11
  7 - MISO to Arduino pin 12
  8 - UNUSED
  add led on pin 5 if needed with 220 ohm resistor to ground

custom parts:
  NRF24L01: NRF24L01 module
