# Fritzing sketch SquishyDrumForKit (saved by Fritzing 0.9.3b)
stripboards: 1

parts:
  NRF24L1 = NRF24L01
  U2 = SWITCH_SPDT [package=kps-1290]
  VCC1 = Battery block 9V
  J4 = Basic Force Sensing Resistor (FSR) [package=THT]
  J5 = Basic Force Sensing Resistor (FSR) [package=THT]
  J6 = Basic Force Sensing Resistor (FSR) [package=THT]
  R9 = Resistor [tolerance=±5% resistance=10k package=THT]
  R10 = Resistor [tolerance=±5% resistance=10k package=THT]
  R11 = Resistor [tolerance=±5% resistance=10k package=THT]
  Part2 = Arduino Pro Mini (3.3V)
  J7 = Piezo Speaker
  J8 = Piezo Speaker
  R12 = Resistor [tolerance=±5% resistance=1M package="0402 [SMD]"]
  R13 = Resistor [tolerance=±5% resistance=1M package="0402 [SMD]"]

nets:
  VCC: NRF24L1.VCC, J5.pin_0, Part2.VCC
  N1: NRF24L1.CSN, Part2.D10
  N2: NRF24L1.MOSI, Part2.MOSI
  GND: NRF24L1.GND, VCC1.-, R11.Pin_1, Part2.GND, R12.Pin_0, R13.Pin_0
  N3: NRF24L1.CE, Part2.D9
  N4: NRF24L1.SCK, Part2.SCK
  N5: NRF24L1.MISO, Part2.MISO
  N6: U2.O, VCC1.+
  N7: U2.P, Part2.RAW
  N8: J4.pin_1, R10.Pin_0, Part2.A1
  N9: J5.pin_1, R11.Pin_0, Part2.A0
  N10: J6.pin_1, R9.Pin_0, Part2.A2
  N11: Part2.A4, J7.pin2
  N12: Part2.A3, J8.pin2

notes:
  FSRs on A1, A3, A4
  Pro Mini 3.3v 8mHz 328 chipset
  NRF connections
  1 - GND
  2 - VCC 3.3V !!! NOT 5V
  3 - CE to Arduino pin 9
  4 - CSN to Arduino pin 10
  5 - SCK to Arduino pin 13
  6 - MOSI to Arduino pin 11
  7 - MISO to Arduino pin 12
  8 - UNUSED
  add led on pin 5 if needed with 220 ohm resistor to ground
  sends
  #define JOYSTICK_X A0 fsr
  #define JOYSTICK_Y A1 fsr
  #define JOYSTICK_Z A2 fsr
  #define JOYSTICK_A A3 piezo
  #define JOYSTICK_B A4 piezo
  #define JOYSTICK_C A7 n/a

custom parts:
  NRF24L01: NRF24L01 module
