# Fritzing sketch NoodlerForKit (saved by Fritzing 0.9.3b)

parts:
  NRF24L1 = NRF24L01
  U2 = SWITCH_SPDT [package=kps-1290]
  VCC1 = Battery block 9V
  U3 = Wiichuck Adapter
  Part2 = Arduino Pro Mini (3.3V)

nets:
  VCC: NRF24L1.VCC, Part2.VCC
  N1: NRF24L1.CSN, Part2.D10
  N2: NRF24L1.MOSI, Part2.MOSI
  GND: NRF24L1.GND, VCC1.-, Part2.GND
  N3: NRF24L1.CE, Part2.D9
  N4: NRF24L1.SCK, Part2.SCK
  N5: NRF24L1.MISO, Part2.MISO
  N6: U2.O, Part2.RAW
  N7: U2.P, VCC1.+
  N8: U3.-, Part2.A2
  N9: U3.+, Part2.A3
  N10: U3.SDA, Part2.A4
  N11: U3.SCL, Part2.A5

notes:
  Pro Mini 3.3v 8mHz 328 chipset
  NRF connections
  1 - GND
  2 - VCC 3.3V !!! NOT 5V
  3 - CE to Arduino pin 9
  4 - CSN to Arduino pin 10
  5 - SCK to Arduino pin 13
  6 - MOSI to Arduino pin 11
  7 - MISO to Arduino pin 12
  8 - UNUSED
  add led on pin 5 if needed with 220 ohm resistor to ground
  My nunchuck clone wiring pinout is as follows
  white (purple in fritzing) A5 c
  yellow actual cable (blue in fritzing) A4 d
  green A3 vcc
  red A2 gnd
  nunchuck output from arduino is x y z zbut cbut joyx joyy

custom parts:
  NRF24L01: NRF24L01 module
  Wiichuck Adapter: SCP1000 Barometric Pressure sensor. Can sense air pressure and temperature. SPI interface.
