# Fritzing sketch ReceiversForKit (saved by Fritzing 0.9.3b)

parts:
  Part1 = Arduino Nano (Rev3.0)
  NRF24L2 = NRF24L01

nets:
  GND: Part1.GND, NRF24L2.GND
  N1: Part1.D9, Part1.5V, NRF24L2.CE
  N2: Part1.D10, NRF24L2.CSN
  N3: Part1.D11/MOSI, NRF24L2.MOSI
  N4: Part1.D12/MISO, NRF24L2.MISO
  3V3: Part1.3V3, NRF24L2.VCC
  N5: Part1.D13/SCK, NRF24L2.SCK

notes:
  Arduino Nano 328 chipset
  drivers from http://rebrand.ly/b35d
  or
  https://sparks.gogo.co.nz/ch340.html
  NRF connections
  1 - GND
  2 - VCC 3.3V !!! NOT 5V
  3 - CE to Arduino pin 9
  4 - CSN to Arduino pin 10
  5 - SCK to Arduino pin 13
  6 - MOSI to Arduino pin 11
  7 - MISO to Arduino pin 12
  8 - UNUSED

custom parts:
  NRF24L01: NRF24L01 module
