# Fritzing sketch TouchBoxForKit (saved by Fritzing 0.9.3b)
stripboards: 1
perfboards: 1

parts:
  Teensy_3_1 = Teensy 3.1  # not connected
  Board1 = Teensy audio shield [chip_label=IC package="DIP (Dual Inline) [THT]"]
  Part4 = Mono Audio Amp Breakout
  SP1 = SPEAKER [package=pcb_mount_speaker]
  VCC1 = Battery
  S1 = Round Pushbutton
  S2 = Round Pushbutton
  S3 = Round Pushbutton
  S4 = Round Pushbutton
  S5 = Round Pushbutton
  R1 = Rotary Potentiometer (Large) [maximum_resistance=10kΩ package=THT]
  R2 = Rotary Potentiometer (Large) [maximum_resistance=10kΩ package=THT]
  LCD2 = LCD screen
  LCM1602_IIC2 = LCM1602 IIC [part_number="LCM1602 IIC" chip_label="LCM1602 IIC" package="DIP (Dual Inline) [THT]"]
  S7 = Toggle Switch [package=THT]
  U1 = CAPSENSE_PAD [package=capsense_pad]  # not connected
  TRS1 = Audio Jack (TRS) 3.5mm [package="PG203J [THT]"]  # not connected
  U2 = CAPSENSE_PAD [package=capsense_pad]  # not connected
  U3 = CAPSENSE_PAD [package=capsense_pad]  # not connected
  U4 = CAPSENSE_PAD [package=capsense_pad]  # not connected
  U5 = CAPSENSE_PAD [package=capsense_pad]  # not connected
  U6 = CAPSENSE_PAD [package=capsense_pad]
  U7 = CAPSENSE_PAD [package=capsense_pad]  # not connected
  U8 = CAPSENSE_PAD [package=capsense_pad]  # not connected
  g1 = AMPHENOL - ACJS-MHDR [package=ACJS-MHDR]
  S8 = SWITCH-DPDT [package=os]
  Part5 = NCP1400 Step-Up Breakout

nets:
  VCC: Board1.VCC, R1.leg1, R2.leg1, S8.5, Part5.VIN
  N1: Board1.SCL, LCM1602_IIC2.SCL
  N2: Board1.SDA, LCM1602_IIC2.SDA
  N3: Board1.VOL, U6.RECEIVE
  GND: Board1.GND, Part4.GND, VCC1.-, S1.leg1, S2.leg1, S3.leg1, S4.leg1, S5.leg1, LCM1602_IIC2.GND, Part5.GND
  N4: Part4.OUT+, SP1.-
  N5: Part4.OUT-, SP1.+
  N6: Part4.VIN, S8.4
  N7: VCC1.+, S7.COM
  N8: R1.leg2, R2.leg2
  VSS: LCD2.VSS, LCM1602_IIC2.VSS
  VDD: LCD2.VDD, LCM1602_IIC2.VDD
  N9: LCD2.V0, LCM1602_IIC2.V0
  N10: LCD2.RS, LCM1602_IIC2.RS
  N11: LCD2.R/W, LCM1602_IIC2.RW
  N12: LCD2.E, LCM1602_IIC2.E
  N13: LCD2.DB0, LCM1602_IIC2.D0
  N14: LCD2.DB1, LCM1602_IIC2.D1
  N15: LCD2.DB2, LCM1602_IIC2.D2
  N16: LCD2.DB3, LCM1602_IIC2.D3
  N17: LCD2.DB4, LCM1602_IIC2.D4
  N18: LCD2.DB5, LCM1602_IIC2.D5
  N19: LCD2.DB6, LCM1602_IIC2.D6
  N20: LCD2.DB7, LCM1602_IIC2.D7
  N21: LCD2.LED+, LCM1602_IIC2.A
  N22: LCD2.LED-, LCM1602_IIC2.K
  N23: LCM1602_IIC2.VCC, Part5.VOUT
  N24: LCM1602_IIC2.LED_A, LCM1602_IIC2.LED_B
  N25: g1.Ring_(5), g1.Tip_(6), S8.1

notes:
  perfboard next to the teensy audio represents the back side holes
  25, 32, 33, A10, A13, 29
  step up from 1-4v to 5v for screen

custom parts:
  Teensy audio shield: https://www.pjrc.com/store/teensy3_audio.html
  Mono Audio Amp Breakout: Description: This tiny audio amplifier is based on the Texas Instruments TPA2005D1. Its efficient class-D operation means low heat and long battery life. It can drive an 8-Ohm speaker at up to 1.4 Watts; it won't shake a stadium, but it will provide plenty of volume for your audio projects. The fully-differential inputs are safe for floating audio signals such as from our MP3 Shield, and can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
  LCM1602 IIC: I2C-Module to use a 1602 or 2004 LCD on with the wire.h libory Serial LCD Modul
